# Fritzing sketch Integration Schematics (saved by Fritzing 0.9.4)
breadboards: 1

parts:
  Altimeter_MS5607 = mystery part, 7 pins [chip_label=Altitude]
  SIM33EAU_GPS_Module = mystery part, 4 pins [chip_label=GPS]
  TNC = mystery part, 4 pins [chip_label=TNC]
  Battery = Battery
  Temperature_MAX31865 = mystery part, 6 pins [chip_label=Temperature]
  OV5642_Camera_Module = IC, SIP package, 8 pins [chip_label=OV5642]
  part = Arduino Mega 2560 (Rev3)
  MicroSD_Module = Adafruit MicroSD card breakout board [part_number="Adafruit #254"]
  Power_Indicator = LEDs [package=led10mm]
  Power_Switch = SPST Switch [package=switch-spdt-smd]
  R1 = Resistor [tolerance=±5% resistance=470 package=THT]
  ANTENNA = Antenna
  J2 = female pin header, 3 pins [form="♀ (female)"]
  SMA_OUT1 = SMA Antenna Connector [package=sma-edge]
  U2 = RELAY [package=relay-t9a]
  Transistor1 = NPN-Transistor [package="TO92 [THT]"]
  D54 = Diode [package=diode-1n4001]
  R2 = Resistor [tolerance=±5% resistance=220 package=THT]
  APRS = mystery part, 5 pins [chip_label=APRS]

nets:
  GND: Altimeter_MS5607.pin1, SIM33EAU_GPS_Module.pin4, TNC.pin4, Battery.-, Temperature_MAX31865.pin6, OV5642_Camera_Module.pin5, part.GND, MicroSD_Module.GND, Power_Indicator.C, Power_Switch.S, J2.pin3, Transistor1.E, APRS.pin2
  3.3V: Altimeter_MS5607.pin2, TNC.pin1, part.3V3, MicroSD_Module.+3V3
  SCL: Altimeter_MS5607.pin4, OV5642_Camera_Module.pin8, MicroSD_Module.CLK
  SDA: Altimeter_MS5607.pin5, OV5642_Camera_Module.pin7, part.D20/SDA
  D14: SIM33EAU_GPS_Module.pin1, part.D14/TX3
  D15: SIM33EAU_GPS_Module.pin2, part.D15/RX3
  5V: SIM33EAU_GPS_Module.pin3, Temperature_MAX31865.pin1, OV5642_Camera_Module.pin6, part.5V
  D18: TNC.pin2, part.D18/TX1
  D19: TNC.pin3, part.D19/RX1
  N1: Battery.+, Power_Switch.P
  SCK: Temperature_MAX31865.pin2, OV5642_Camera_Module.pin4, part.D52
  MISO: Temperature_MAX31865.pin3, OV5642_Camera_Module.pin3, part.D50, MicroSD_Module.DO
  MOSI: Temperature_MAX31865.pin4, OV5642_Camera_Module.pin2, part.D51, MicroSD_Module.DI
  D10: Temperature_MAX31865.pin5, part.D10_PWM
  D7: OV5642_Camera_Module.pin1, part.D8_PWM
  BAT+: part.VIN, Power_Switch.O, R1.Pin_0
  D23: part.D23
  D53: part.D53, MicroSD_Module.CS
  N2: Power_Indicator.A, R1.Pin_1
  N3: ANTENNA.antenna_lead, SMA_OUT1.SIGNAL
  APRS LED: J2.pin1, R2.Pin_0, APRS.pin5
  5V out: J2.pin2, U2.COIL2, D54.A, APRS.pin4
  N4: SMA_OUT1.GND, U2.MAIN
  N5: U2.COIL1, Transistor1.C, D54.C
  Handheld Radio Signal: U2.NC
  APRS Signal: U2.NO
  TX: APRS.pin1
  9V: APRS.pin3

notes:
  VisonSat2020, Author: Alex Tate, 5

custom parts:
  Battery: Your standard 2x 18650 battery pack (7,4 Volts)
  Adafruit MicroSD card breakout board: Not just a simple breakout board, this microSD adapter goes the extra mile - designed for ease of use. Onboard 5v->3v regulator provides 150mA for power-hungry cards 3v level shifting means you can use this with ease on either 3v or 5v systems Uses a proper level shifting chip, not resistors: less problems, and faster read/write access Use 3 or 4 digital pins to read and write 2Gb+ of storage!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
