# Fritzing sketch wiring_diagram (saved by Fritzing 0.9.4)
breadboards: 1

parts:
  U1 = mystery part, 1 pin [chip_label=5V part_number=VIN]
  U2 = mystery part, 1 pin [chip_label=D50 part_number=MISO]
  U3 = mystery part, 1 pin [chip_label=D52 part_number=SCK]
  U4 = mystery part, 1 pin [chip_label=SDA part_number=SDA]
  U5 = mystery part, 1 pin [chip_label="9 - 12V" part_number="BAT V+"]
  U6 = mystery part, 1 pin [chip_label=GND part_number=GND]
  U7 = mystery part, 1 pin [chip_label=MOSI part_number=D51]
  U8 = mystery part, 1 pin [chip_label=SCL(8) part_number=SCL]
  U10 = mystery part, 1 pin [chip_label=D52 part_number=CLK]
  U13 = mystery part, 1 pin [chip_label=D52 part_number=MISO]
  U14 = mystery part, 1 pin [chip_label=5V part_number=5V]
  U15 = mystery part, 1 pin [chip_label=D51 part_number=MOSI]
  U16 = mystery part, 1 pin [chip_label=GND part_number=GND]
  U17 = mystery part, 1 pin [chip_label=GND part_number=GND]
  U18 = mystery part, 1 pin [chip_label=3.3V part_number=3.3V]
  U19 = mystery part, 1 pin [chip_label=RX part_number=D18]
  U20 = mystery part, 1 pin [chip_label=TX part_number=D19]
  U21 = mystery part, 1 pin [chip_label=RXD part_number=D14]
  U22 = mystery part, 1 pin [chip_label=TXD part_number=D15]
  U23 = mystery part, 1 pin [chip_label=GND part_number=GND]
  U24 = mystery part, 1 pin [chip_label=VIN part_number=5V]
  U25 = mystery part, 1 pin [chip_label=SDA part_number=SDA]
  U26 = mystery part, 1 pin [chip_label=SCL part_number=SCL]
  U27 = mystery part, 1 pin [chip_label=GND part_number=GND]
  U28 = mystery part, 1 pin [chip_label=VIN part_number=3.3V]
  U29 = mystery part, 1 pin [chip_label=3.3V part_number=3.3V]
  U30 = mystery part, 1 pin [chip_label=CLK part_number=SCL?]
  U31 = mystery part, 1 pin [chip_label=DI part_number=D51]
  U32 = mystery part, 1 pin [chip_label=GND part_number=GND]
  U33 = mystery part, 1 pin [chip_label=CS part_number=D53]
  U34 = mystery part, 1 pin [chip_label=DO part_number=D50]
  U35 = mystery part, 1 pin [chip_label=SCL part_number=SCL]
  U36 = mystery part, 1 pin [chip_label=RX part_number="TX ON GPS"]
  U37 = mystery part, 1 pin [chip_label=VIN part_number=3.3V]
  U38 = mystery part, 1 pin [chip_label=D7 part_number=CS]
  U39 = mystery part, 1 pin [chip_label=GND part_number="BAT G"]

nets:
  N1: U1.pin1, U2.pin1, U3.pin1, U4.pin1, U5.pin1, U6.pin1, U7.pin1, U8.pin1, U38.pin1, U39.pin1
  N2: U10.pin1, U13.pin1, U14.pin1, U15.pin1, U16.pin1
  N3: U17.pin1, U18.pin1, U19.pin1, U20.pin1
  N4: U21.pin1, U22.pin1, U23.pin1, U24.pin1
  N5: U25.pin1, U26.pin1, U27.pin1, U28.pin1
  N6: U29.pin1, U30.pin1, U31.pin1, U32.pin1, U33.pin1, U34.pin1
  N7: U35.pin1, U36.pin1, U37.pin1

notes:
  Camera
  Temp
  TNC
  GPS
  Altimeter
  SD
  APRS
